# Fritzing sketch Exp4th (saved by Fritzing 0.9.4)
breadboards: 1

parts:
  U1 = M74HC238 [package=dil16]
  U2 = M74HC238 [package=dil16]
  U5 = 7495 [package="DIP14 [THT]"]
  LED1 = smd LED [color="Red (633nm)" package="1206 [SMD]"]
  LED2 = smd LED [color="Red (633nm)" package="1206 [SMD]"]
  LED3 = smd LED [color="Red (633nm)" package="1206 [SMD]"]
  LED4 = smd LED [color="Red (633nm)" package="1206 [SMD]"]
  U6 = 74HC04_HEX_INVERTER [package=dil14]
  IC1 = 74HC08 Logic AND Gate [part_number=74HC08 package="DIP (Dual Inline) [THT]"]
  LED5 = smd LED [color="Red (633nm)" package="1206 [SMD]"]

nets:
  N1: U1.A, U2.A, U2.~G2A, U5.6A, LED1.cathode, U6.6A
  N2: U1.B, U2.B, U5.6Y, LED2.cathode
  N3: U1.C, U2.C, U5.5A, LED3.cathode
  N4: U1.~G2A, U6.6Y
  GND: U1.GND, U2.GND, U5.2A, U5.3A, U5.GND, LED2.anode, LED3.anode, U6.GND, IC1.GND, LED5.anode
  N5: U1.Y5, IC1.3A
  N6: U1.Y4, IC1.3B
  VCC: U1.VCC, U2.VCC, U5.1A, U5.1Y, U5.2Y, U5.3Y, U5.VCC, U6.VCC, IC1.VCC
  N7: U2.Y2, IC1.4A
  N8: U2.Y1, IC1.4B
  N9: U5.5Y, LED4.cathode
  N10: U6.1A, IC1.1Y
  N11: U6.1Y, LED5.cathode
  N12: IC1.1A, IC1.4Y
  N13: IC1.1B, IC1.3Y

notes:
  Clock input

custom parts:
  7495: Hex Inverter Schmitt Trigger
