# Fritzing sketch Exp6th (saved by Fritzing 0.9.4)
breadboards: 2

parts:
  U1 = M74HC238 [package=dil16]
  U2 = M74HC238 [package=dil16]
  LED1 = LED - 3mm [color="Red (633nm)" package="3 mm [THT]"]
  LED2 = LED - 3mm [color="Red (633nm)" package="3 mm [THT]"]
  LED3 = LED - 3mm [color="Red (633nm)" package="3 mm [THT]"]
  LED4 = LED - 3mm [color="Red (633nm)" package="3 mm [THT]"]
  LED5 = LED - 3mm [color="Red (633nm)" package="3 mm [THT]"]
  U3 = 4071 4 x 2 Input OR Gate, multi-part [part_number=4071 package="DIP (Dual Inline) [THT]"]
  part = 4071_4_x_2_input_OR_gate_multipart_subpart1 [part_number=4071]  # not connected
  U3_1 = 4071_4_x_2_input_OR_gate_multipart_subpart2 [part_number=4071]  # not connected
  U3_2 = 4071_4_x_2_input_OR_gate_multipart_subpart3 [part_number=4071]  # not connected
  U3_3 = 4071_4_x_2_input_OR_gate_multipart_subpart4 [part_number=4071]  # not connected
  U3_4 = 4071_4_x_2_input_OR_gate_multipart_subpart5 [part_number=4071]  # not connected
  U4 = 4071 4 x 2 Input OR Gate, multi-part [part_number=4071 package="DIP (Dual Inline) [THT]"]
  part_2 = 4071_4_x_2_input_OR_gate_multipart_subpart1 [part_number=4071]  # not connected
  U4_1 = 4071_4_x_2_input_OR_gate_multipart_subpart2 [part_number=4071]  # not connected
  U4_2 = 4071_4_x_2_input_OR_gate_multipart_subpart3 [part_number=4071]  # not connected
  U4_3 = 4071_4_x_2_input_OR_gate_multipart_subpart4 [part_number=4071]  # not connected
  U4_4 = 4071_4_x_2_input_OR_gate_multipart_subpart5 [part_number=4071]  # not connected
  LED6 = LED - 3mm [color="Red (633nm)" package="3 mm [THT]"]
  CD4048B1 = CD4048B [part_number=CD4048B package="DIP (Dual Inline) [THT]"]
  U5 = SN74LS14N [package="DIP14 [THT]"]
  CD4048B2 = CD4048B [part_number=CD4048B package="DIP (Dual Inline) [THT]"]
  U6 = 74HC595 [package="DIP16 [THT]"]
  U7 = 4070 4 x 2 Input XOR Gate, multi-part [part_number=4070 package="DIP (Dual Inline) [THT]"]
  part_3 = 4070_4_x_2_input_XOR_gate_multipart_subpart1 [part_number=4070]  # not connected
  U7_1 = 4070_4_x_2_input_XOR_gate_multipart_subpart2 [part_number=4070]  # not connected
  U8 = 4070_4_x_2_input_XOR_gate_multipart_subpart2 [part_number=4070]
  U8_2 = 4077_4_x_2_input_XNOR_gate_multipart_subpart5 [part_number=4077]
  U9 = 4081 4 x 2 Input AND Gate, multi-part [part_number=4081 package="DIP (Dual Inline) [THT]"]
  part_4 = 4081_4_x_2_input_AND_gate_multipart_subpart1 [part_number=4081]  # not connected
  U9_1 = 4081_4_x_2_input_AND_gate_multipart_subpart2 [part_number=4081]  # not connected
  U9_2 = 4081_4_x_2_input_AND_gate_multipart_subpart3 [part_number=4081]  # not connected
  U9_4 = 4081_4_x_2_input_AND_gate_multipart_subpart5 [part_number=4081]  # not connected

nets:
  N1: U1.A, U2.A, CD4048B1.A
  N2: U1.B, U2.B, CD4048B1.B
  N3: U1.C, U2.C, CD4048B1.C
  VCC: U1.~G2A, U1.~G2B, U1.VCC, U2.~G2A, U2.~G2B, U2.VCC, U3.connector13, U4.connector13
  N4: U1.G1, U5.4Y
  N5: U1.Y7, U4.connector0
  GND: U1.GND, U2.GND, LED1.anode, LED2.anode, LED3.anode, LED4.anode, LED5.anode, U3.connector6, U4.connector6, LED6.anode
  N6: U1.Y6, U4.connector1
  N7: U1.Y5, U4.connector7
  N8: U1.Y4, U4.connector4
  N9: U1.Y3, U4.connector5
  N10: U1.Y2, U4.connector11, U9.connector4
  N11: U1.Y1, U4.connector12
  N12: U1.Y0, LED5.cathode
  N13: U2.G1, CD4048B1.D, U5.4A
  N14: U2.Y5, U3.connector7, U5.3A
  N15: U2.Y4, U3.connector11
  N16: U2.Y3, U3.connector12
  N17: U2.Y2, U3.connector1
  N18: U2.Y1, U3.connector0
  N19: U2.Y0, U3.connector4
  N20: LED1.cathode, U3.connector2
  N21: LED2.cathode, U3.connector3
  N22: LED3.cathode, U4.connector9
  N23: LED4.cathode, U4.connector10
  N24: U3.connector5, U4.connector2
  N25: U3.connector8, U8_2.connector10, U9.connector10
  N26: U3.connector9, CD4048B2.B
  N27: U3.connector10, LED6.cathode
  N28: U4.connector3, U4.connector8
  N29: CD4048B1.J, U5.3Y
  N30: CD4048B1.Kd, U6.Q3
  VDD: CD4048B1.H, CD4048B1.E, CD4048B1.VDD, U5.VCC, CD4048B2.VDD, U6.VCC, U7.connector13, U9.connector13
  VSS: CD4048B1.G, CD4048B1.F, CD4048B1.VSS, CD4048B1.Ka, U5.GND, CD4048B2.VSS, CD4048B2.Ka, CD4048B2.D, U6.GND, U7.connector6, U9.connector6
  N31: CD4048B1.Kb, CD4048B2.EXPAND
  N32: CD4048B1.Kc, U5.6Y
  N33: U5.6A, U9.connector3
  N34: U6.Q1, U7.connector0
  N35: U6.Q5, U7.connector1
  N36: U7.connector2, U8_2.connector12, U9.connector12
  N37: U8.connector0, U9.connector0
  N38: U8.connector1, U9.connector1
  N39: U8.connector2, U8_2.connector11, U9.connector2, U9.connector11

notes:
  clock input
  start
  mode
  door
  water
