# Fritzing sketch Exp7th (saved by Fritzing 0.9.4)
breadboards: 3

parts:
  LED1 = LED - 5mm [color="Red (633nm)" package="5 mm [THT]"]
  LED2 = LED - 5mm [color="Red (633nm)" package="5 mm [THT]"]
  U1 = HEF4543 [package=dil16]
  U2 = HEF4543 [package=dil16]
  7_Segment1 = 7 Segment Display
  7_Segment2 = 7 Segment Display
  U3 = 4081 4 x 2 Input AND Gate, multi-part [part_number=4081 package="DIP (Dual Inline) [THT]"]
  part = 4081_4_x_2_input_AND_gate_multipart_subpart1 [part_number=4081]  # not connected
  U3_1 = 4081_4_x_2_input_AND_gate_multipart_subpart2 [part_number=4081]  # not connected
  U3_2 = 4081_4_x_2_input_AND_gate_multipart_subpart3 [part_number=4081]  # not connected
  U3_3 = 4081_4_x_2_input_AND_gate_multipart_subpart4 [part_number=4081]  # not connected
  U3_4 = 4081_4_x_2_input_AND_gate_multipart_subpart5 [part_number=4081]  # not connected
  U4 = 4071 4 x 2 Input OR Gate, multi-part [part_number=4071 package="DIP (Dual Inline) [THT]"]
  part_2 = 4071_4_x_2_input_OR_gate_multipart_subpart1 [part_number=4071]  # not connected
  U4_1 = 4071_4_x_2_input_OR_gate_multipart_subpart2 [part_number=4071]  # not connected
  U4_2 = 4071_4_x_2_input_OR_gate_multipart_subpart3 [part_number=4071]  # not connected
  U4_3 = 4071_4_x_2_input_OR_gate_multipart_subpart4 [part_number=4071]  # not connected
  U4_4 = 4071_4_x_2_input_OR_gate_multipart_subpart5 [part_number=4071]  # not connected
  IC2 = IC, DIP package, 14 pins [chip_label="D latch"]
  U5 = 4070 4 x 2 Input XOR Gate, multi-part [part_number=4070 package="DIP (Dual Inline) [THT]"]
  part_3 = 4070_4_x_2_input_XOR_gate_multipart_subpart1 [part_number=4070]  # not connected
  U5_4 = 4070_4_x_2_input_XOR_gate_multipart_subpart5 [part_number=4070]  # not connected
  IC3 = IC, DIP package, 14 pins [chip_label=or_4]
  U6 = SN74LS14N [package="DIP14 [THT]"]
  IC4 = IC, DIP package, 16 pins [chip_label="JK latch"]
  U7 = 4081 4 x 2 Input AND Gate, multi-part [part_number=4081 package="DIP (Dual Inline) [THT]"]
  part_4 = 4081_4_x_2_input_AND_gate_multipart_subpart1 [part_number=4081]  # not connected
  U7_1 = 4081_4_x_2_input_AND_gate_multipart_subpart2 [part_number=4081]  # not connected
  U7_3 = 4081_4_x_2_input_AND_gate_multipart_subpart4 [part_number=4081]  # not connected
  U7_4 = 4081_4_x_2_input_AND_gate_multipart_subpart5 [part_number=4081]  # not connected
  IC5 = IC, DIP package, 14 pins [chip_label="D latch"]
  IC6 = IC, DIP package, 14 pins [chip_label="D latch"]

nets:
  N1: LED1.cathode, U6.2A, IC4.pin5, U7.connector2, U7.connector11
  GND: LED1.anode, LED2.anode, U1.LD, U1.GND, U1.A, U2.LD, U2.GND, U2.A, 7_Segment1.Segment_D, U3.connector6, U4.connector6, IC2.pin7, U5.connector6, IC3.pin7, U6.GND, IC4.pin8, U7.connector6, IC5.pin7, IC6.pin7
  N2: LED2.cathode, U4.connector12, U6.1Y, U7.connector12
  N3: U1.D2, 7_Segment1.Segment_E, U3.connector0, IC3.pin5
  N4: U1.D0, U4.connector2
  N5: U1.PH, U1.C, 7_Segment1.Segment_G, 7_Segment1.Segment_F, U3.connector1, IC3.pin3, IC3.pin4
  N6: U1.BL, U4.connector8
  N7: U1.B, U2.B, U5.connector10, U6.6A
  N8: U1.G, 7_Segment1.common_anode, IC3.pin2
  N9: U1.F, U2.F, IC2.pin11, IC4.pin15
  VCC: U1.VCC, U2.VCC, 7_Segment1.Segment_B, 7_Segment1.Segment_A, U3.connector13, U4.connector13, IC2.pin14, U5.connector13, IC3.pin14, U6.VCC, IC4.pin10, IC4.pin11, IC4.pin16, U7.connector13, IC5.pin14, IC6.pin14
  N10: U2.D2, 7_Segment2.Segment_E, U3.connector5, IC3.pin12
  N11: U2.D0, U4.connector9
  N12: U2.PH, U2.C, 7_Segment2.Segment_G, 7_Segment2.Segment_F, U3.connector4, IC3.pin9, IC3.pin11
  N13: U2.E, 7_Segment2.common_anode, IC3.pin10
  N14: 7_Segment2.Segment_B, 7_Segment2.Segment_A
  N15: U3.connector2, U3.connector8
  N16: U3.connector3, U3.connector7
  N17: U3.connector9, U3.connector12, U4.connector7
  N18: U3.connector10, U4.connector0
  N19: U3.connector11, U4.connector11, U6.2Y
  N20: U4.connector1, U7.connector9
  N21: U4.connector3, U6.1A
  N22: U4.connector4, IC3.pin1
  N23: U4.connector5, IC3.pin13
  N24: U4.connector10, U7.connector7
  N25: IC2.pin9, U5.connector12
  N26: IC2.pin13, U5.connector11
  N27: U6.4Y, IC4.pin4
  N28: U6.4A, U7.connector1
  N29: U6.6Y, U7.connector8
  N30: IC4.pin2, U7.connector0
  N31: IC4.pin3, IC4.pin13
  N32: IC4.pin6, IC6.pin1
  N33: IC5.pin1, IC5.pin9
  N34: IC5.pin3, IC5.pin11, IC6.pin3
  N35: IC5.pin13, IC6.pin5

notes:
  call status
  warning
  coin
  clock
  start
