# Fritzing sketch Exp8th (saved by Fritzing 0.9.4)
breadboards: 2

parts:
  IC1 = IC, DIP package, 24 pins [chip_label=74181]
  U1 = 4081 4 x 2 Input AND Gate, multi-part [part_number=4081 package="DIP (Dual Inline) [THT]"]
  part = 4081_4_x_2_input_AND_gate_multipart_subpart1 [part_number=4081]  # not connected
  U1_1 = 4081_4_x_2_input_AND_gate_multipart_subpart2 [part_number=4081]  # not connected
  U1_2 = 4081_4_x_2_input_AND_gate_multipart_subpart3 [part_number=4081]  # not connected
  U1_3 = 4081_4_x_2_input_AND_gate_multipart_subpart4 [part_number=4081]  # not connected
  U1_4 = 4081_4_x_2_input_AND_gate_multipart_subpart5 [part_number=4081]  # not connected
  U2 = 4071 4 x 2 Input OR Gate, multi-part [part_number=4071 package="DIP (Dual Inline) [THT]"]
  part_2 = 4071_4_x_2_input_OR_gate_multipart_subpart1 [part_number=4071]  # not connected
  U2_1 = 4071_4_x_2_input_OR_gate_multipart_subpart2 [part_number=4071]  # not connected
  U2_3 = 4071_4_x_2_input_OR_gate_multipart_subpart4 [part_number=4071]  # not connected
  U2_4 = 4071_4_x_2_input_OR_gate_multipart_subpart5 [part_number=4071]  # not connected
  U3 = SN74LS14N [package="DIP14 [THT]"]
  IC3 = IC, DIP package, 16 pins [chip_label=74175]
  IC2 = IC, DIP package, 16 pins [chip_label=74175]
  U4 = SN74LS14N [package="DIP14 [THT]"]
  U5_3 = 4081_4_x_2_input_AND_gate_multipart_subpart4 [part_number=4081]  # not connected
  U5_2 = 4081_4_x_2_input_AND_gate_multipart_subpart3 [part_number=4081]  # not connected
  part_3 = 4081_4_x_2_input_AND_gate_multipart_subpart1 [part_number=4081]  # not connected
  U5 = 4081 4 x 2 Input AND Gate, multi-part [part_number=4081 package="DIP (Dual Inline) [THT]"]
  U5_1 = 4081_4_x_2_input_AND_gate_multipart_subpart2 [part_number=4081]  # not connected
  U6_3 = 4081_4_x_2_input_AND_gate_multipart_subpart4 [part_number=4081]  # not connected
  U6_2 = 4081_4_x_2_input_AND_gate_multipart_subpart3 [part_number=4081]  # not connected
  U6 = 4081 4 x 2 Input AND Gate, multi-part [part_number=4081 package="DIP (Dual Inline) [THT]"]
  U6_1 = 4081_4_x_2_input_AND_gate_multipart_subpart2 [part_number=4081]  # not connected
  U7_3 = 4071_4_x_2_input_OR_gate_multipart_subpart4 [part_number=4071]  # not connected
  U7_4 = 4071_4_x_2_input_OR_gate_multipart_subpart5 [part_number=4071]  # not connected
  U7_2 = 4071_4_x_2_input_OR_gate_multipart_subpart3 [part_number=4071]  # not connected
  part_4 = 4071_4_x_2_input_OR_gate_multipart_subpart1 [part_number=4071]  # not connected
  U7 = 4071 4 x 2 Input OR Gate, multi-part [part_number=4071 package="DIP (Dual Inline) [THT]"]
  U7_1 = 4071_4_x_2_input_OR_gate_multipart_subpart2 [part_number=4071]  # not connected
  U8_1 = 4081_4_x_2_input_AND_gate_multipart_subpart2 [part_number=4081]  # not connected
  U8_4 = 4081_4_x_2_input_AND_gate_multipart_subpart5 [part_number=4081]  # not connected
  U8_3 = 4081_4_x_2_input_AND_gate_multipart_subpart4 [part_number=4081]  # not connected
  U8 = 4081 4 x 2 Input AND Gate, multi-part [part_number=4081 package="DIP (Dual Inline) [THT]"]
  U8_2 = 4081_4_x_2_input_AND_gate_multipart_subpart3 [part_number=4081]  # not connected
  U9 = SN74LS14N [package="DIP14 [THT]"]

nets:
  N1: IC1.pin1, IC2.pin3
  N2: IC1.pin2, IC3.pin3
  VCC: IC1.pin3, IC1.pin24, U1.connector13, U2.connector13, U3.VCC, IC3.pin1, IC3.pin16, IC2.pin1, IC2.pin16, U4.VCC, U5.connector13, U6.connector13, U7.connector13, U8.connector13, U9.VCC
  N3: IC1.pin5, U2.connector9
  N4: IC1.pin6, U2.connector10
  GND: IC1.pin7, IC1.pin12, U1.connector6, U2.connector6, U3.GND, IC3.pin8, IC2.pin8, U4.GND, U5.connector6, U6.connector6, U7.connector6, U8.connector6, U9.GND
  N5: IC1.pin8, U1.connector2
  N6: IC1.pin9, U4.6A
  N7: IC1.pin10, U4.5A
  N8: IC1.pin11, U4.4A
  N9: IC1.pin14, U4.1A
  N10: IC1.pin18, IC2.pin14
  N11: IC1.pin19, IC3.pin14
  N12: IC1.pin20, IC2.pin11
  N13: IC1.pin21, IC3.pin11
  N14: IC1.pin22, IC2.pin6
  N15: IC1.pin23, IC3.pin6
  N16: U1.connector0, U2.connector2
  N17: U1.connector1, U3.2A
  N18: U1.connector3, U1.connector11
  N19: U1.connector5, U2.connector1, U3.3A
  N20: U1.connector7, U3.2Y
  N21: U1.connector8, U2.connector7, U3.1Y
  N22: U1.connector9, U1.connector12
  N23: U1.connector10, IC2.pin9
  N24: U2.connector0, U2.connector11, U3.1A
  N25: U2.connector8, U2.connector12, U3.3Y
  N26: IC3.pin4, U7.connector2
  N27: IC3.pin5, U7.connector3
  N28: IC3.pin12, U7.connector9
  N29: IC3.pin13, U7.connector10
  N30: U4.1Y, U6.connector0
  N31: U4.2A, U8.connector7
  N32: U4.3Y, U8.connector8
  N33: U4.4Y, U5.connector0
  N34: U4.5Y, U5.connector5
  N35: U4.6Y, U5.connector7
  N36: U5.connector1, U5.connector4, U5.connector8, U6.connector1, U9.4Y
  N37: U5.connector2, U7.connector7
  N38: U5.connector3, U7.connector5
  N39: U5.connector9, U7.connector0
  N40: U6.connector2, U7.connector12
  N41: U6.connector3, U7.connector11
  N42: U6.connector5, U6.connector8, U8.connector1, U8.connector4, U8.connector10, U9.4A
  N43: U6.connector9, U7.connector8
  N44: U7.connector1, U8.connector2
  N45: U7.connector4, U8.connector3
  N46: U8.connector9, U8.connector11

notes:
  A0 A1
  A3 A2
  S0 S1 S2
  CLOCK
  B0 B1 B2 B3
